// Logisim project Atividade5_Automato.circ as structural Verilog: 1 circuit, main circuit main
module main (
  input  in_1
);

  wire _0_q, _1_q, _2_q, and_1_out, and_2_out, and_3_out, and_4_out, and_5_out, and_6_out, button_1_out,
       clock_1_out, d_ff_1_q, or_1_out, or_2_out, or_3_out, or_4_out, or_5_out, or_6_out, or_7_out;

  or or_1 (or_1_out, _0_q, ~in_1);  // OR_Gate
  or or_2 (or_2_out, ~_0_q, in_1, _1_q);  // OR_Gate
  Button button_1 (.out(button_1_out));
  Clock clock_1 (.out(clock_1_out));
  and and_1 (and_1_out, _1_q, in_1, _0_q);
  and and_2 (and_2_out, or_1_out, or_2_out);
  J_K_Flip_Flop _2 (
    .J(and_1_out), .clk(clock_1_out), .K(and_2_out), .Q(_2_q), .reset(button_1_out));  // open: Qn, preset, en
  or or_3 (or_3_out, _2_q, in_1);
  or or_4 (or_4_out, ~_2_q, ~in_1, _0_q);  // OR_Gate
  and and_3 (and_3_out, _0_q, ~in_1);  // AND_Gate
  and and_4 (and_4_out, or_3_out, or_4_out);
  J_K_Flip_Flop _1 (
    .J(and_3_out), .clk(clock_1_out), .K(and_4_out), .Q(_1_q), .reset(button_1_out));  // open: Qn, preset, en
  or or_5 (or_5_out, ~_2_q, in_1, _1_q);  // OR_Gate
  and and_5 (and_5_out, or_5_out, or_6_out);
  or or_6 (or_6_out, ~in_1, _2_q);  // OR_Gate
  or or_7 (or_7_out, ~_1_q, in_1);  // OR_Gate
  J_K_Flip_Flop _0 (
    .J(and_5_out), .clk(clock_1_out), .K(or_7_out), .Q(_0_q), .reset(button_1_out));  // open: Qn, preset, en
  and and_6 (and_6_out, in_1, _2_q, _1_q, ~_0_q);  // AND_Gate
  D_Flip_Flop d_ff_1 (.clk(clock_1_out), .D(and_6_out), .Q(d_ff_1_q));  // open: Qn, preset, en, reset
  // Probe on d_ff_1_q
endmodule
