// Logisim project P2.circ as structural Verilog: 1 circuit, main circuit main
module main (
  input  in_1
);

  wire _0_q, _1_q, and_1_out, and_2_out, and_3_out, clock_1_out, or_1_out, or_2_out, or_3_out, \Saída_q ,
       \Saída_qn ;

  Clock clock_1 (.out(clock_1_out));
  and and_1 (and_1_out, _1_q, _0_q, in_1);
  J_K_Flip_Flop _2 (.J(and_1_out), .clk(clock_1_out), .K(1'b1));  // open: Q, Qn, preset, en, reset
  and and_2 (and_2_out, _0_q, in_1);
  or or_1 (or_1_out, in_1, _0_q);
  J_K_Flip_Flop _1 (.J(and_2_out), .clk(clock_1_out), .K(or_1_out), .Q(_1_q));  // open: Qn, preset, en, reset
  or or_2 (or_2_out, ~_1_q, ~in_1);  // OR_Gate
  or or_3 (or_3_out, _1_q, in_1);
  J_K_Flip_Flop _0 (.J(and_3_out), .clk(clock_1_out), .K(1'b1), .Q(_0_q));  // open: Qn, preset, en, reset
  and and_3 (and_3_out, or_2_out, or_3_out);
  // Probe on \Saída_q 
  D_Flip_Flop \Saída  (.clk(clock_1_out), .D(and_1_out), .Q(\Saída_q ), .Qn(\Saída_qn ));  // open: preset, en, reset
endmodule
