// Logisim project ativextra06.circ as structural Verilog: 1 circuit, main circuit main
module main (
  input  in_1
);

  wire _0_q, _1_q, _2_q, and_1_out, and_2_out, and_3_out, and_4_out, and_5_out, and_6_out, and_7_out,
       and_8_out, and_9_out, and_10_out, and_11_out, button_1_out, clock_1_out, or_1_out, or_2_out, or_3_out,
       or_4_out;

  Button button_1 (.out(button_1_out));
  Clock clock_1 (.out(clock_1_out));
  or or_1 (or_1_out, ~_2_q, _1_q, in_1);  // OR_Gate
  or or_2 (or_2_out, _0_q, in_1);
  and and_1 (and_1_out, _1_q, _0_q, ~in_1);  // AND_Gate
  and and_2 (and_2_out, or_1_out, or_2_out);
  J_K_Flip_Flop _2 (
    .J(and_1_out), .clk(clock_1_out), .K(and_2_out), .Q(_2_q), .reset(button_1_out));  // open: Qn, preset, en
  and and_3 (and_3_out, _2_q, in_1);
  and and_4 (and_4_out, ~_0_q, in_1);  // AND_Gate
  and and_5 (and_5_out, ~in_1, _0_q, ~_2_q);  // AND_Gate
  and and_6 (and_6_out, _0_q, ~in_1);  // AND_Gate
  or or_3 (or_3_out, and_3_out, and_4_out, and_5_out);
  J_K_Flip_Flop _1 (
    .J(and_6_out), .clk(clock_1_out), .K(or_3_out), .Q(_1_q), .reset(button_1_out));  // open: Qn, preset, en
  and and_7 (and_7_out, in_1, _2_q);
  and and_8 (and_8_out, ~in_1, ~_2_q);  // AND_Gate
  and and_9 (and_9_out, ~_1_q, in_1);  // AND_Gate
  and and_10 (and_10_out, ~in_1, ~_0_q);  // AND_Gate
  J_K_Flip_Flop _0 (
    .J(and_10_out), .clk(clock_1_out), .K(or_4_out), .Q(_0_q), .reset(button_1_out));  // open: Qn, preset, en
  or or_4 (or_4_out, and_7_out, and_8_out, and_9_out);
  and and_11 (and_11_out, ~_0_q, in_1, _1_q, _2_q);  // AND_Gate
  D_Flip_Flop s (.clk(clock_1_out), .D(and_11_out));  // open: Q, Qn, preset, en, reset
endmodule
