// Logisim project circuito.circ as structural Verilog: 1 circuit, main circuit main
module main (
  input  in_1
);

  wire clock_1_out, X0_q, X1_q, X2_q, X3_q, Y1_q, Y2_q, Y3_q;

  D_Flip_Flop X3 (.clk(clock_1_out), .D(in_1), .Q(X3_q));  // open: Qn, preset, en, reset
  D_Flip_Flop X2 (.clk(clock_1_out), .D(X3_q), .Q(X2_q));  // open: Qn, preset, en, reset
  D_Flip_Flop X1 (.clk(clock_1_out), .D(X2_q), .Q(X1_q));  // open: Qn, preset, en, reset
  Clock clock_1 (.out(clock_1_out));
  D_Flip_Flop X0 (.clk(clock_1_out), .D(X1_q), .Q(X0_q));  // open: Qn, preset, en, reset
  D_Flip_Flop Y3 (.clk(clock_1_out), .D(X0_q), .Q(Y3_q));  // open: Qn, preset, en, reset
  D_Flip_Flop Y2 (.clk(clock_1_out), .D(Y3_q), .Q(Y2_q));  // open: Qn, preset, en, reset
  D_Flip_Flop Y1 (.clk(clock_1_out), .D(Y2_q), .Q(Y1_q));  // open: Qn, preset, en, reset
  D_Flip_Flop Y0 (.clk(clock_1_out), .D(Y1_q));  // open: Q, Qn, preset, en, reset
endmodule
