// Logisim project flipflopD-35712.circ as structural Verilog: 1 circuit, main circuit main
module main (
);

  wire and_1_out, and_2_out, button_1_out, clock_1_out, d_ff_1_q, d_ff_1_qn, d_ff_2_q, d_ff_2_qn, d_ff_3_q,
       d_ff_3_qn, or_1_out, or_2_out, or_3_out;

  Clock clock_1 (.out(clock_1_out));
  and and_1 (and_1_out, d_ff_1_q, d_ff_2_qn);
  and and_2 (and_2_out, d_ff_3_q, d_ff_2_q, d_ff_1_qn);
  Button button_1 (.out(button_1_out));
  or or_1 (or_1_out, and_1_out, and_2_out);
  D_Flip_Flop d_ff_1 (
    .clk(clock_1_out), .D(or_1_out), .Q(d_ff_1_q), .Qn(d_ff_1_qn), .reset(button_1_out));  // open: preset, en
  or or_2 (or_2_out, d_ff_2_qn, d_ff_3_qn);
  D_Flip_Flop d_ff_2 (
    .clk(clock_1_out), .D(or_2_out), .Q(d_ff_2_q), .Qn(d_ff_2_qn), .preset(button_1_out));  // open: en, reset
  D_Flip_Flop d_ff_3 (
    .clk(clock_1_out), .D(or_3_out), .Q(d_ff_3_q), .Qn(d_ff_3_qn), .preset(button_1_out));  // open: en, reset
  or or_3 (or_3_out, d_ff_1_q, d_ff_3_qn, d_ff_2_q);
endmodule
