// Logisim project flipflopD-pares.circ as structural Verilog: 1 circuit, main circuit main
module main (
);

  wire _1_q, _1_qn, _2_q, _2_qn, _3_q, _3_qn, and_1_out, and_2_out, button_1_out, clock_1_out, or_1_out,
       or_2_out, or_3_out, or_4_out, or_5_out;

  Clock clock_1 (.out(clock_1_out));
  or or_1 (or_1_out, _3_q, _1_q);
  or or_2 (or_2_out, _3_q, _2_q, _1_qn);
  or or_3 (or_3_out, _1_qn, _2_qn, _3_qn);
  Button button_1 (.out(button_1_out));
  and and_1 (and_1_out, or_1_out, or_2_out, or_3_out);
  D_Flip_Flop _3 (.clk(clock_1_out), .D(and_1_out), .Q(_3_q), .Qn(_3_qn), .reset(button_1_out));  // open: preset, en
  or or_4 (or_4_out, _2_q, _1_q);
  or or_5 (or_5_out, _1_qn, _2_qn);
  D_Flip_Flop _2 (.clk(clock_1_out), .D(and_2_out), .Q(_2_q), .Qn(_2_qn), .reset(button_1_out));  // open: preset, en
  and and_2 (and_2_out, or_4_out, or_5_out);
  D_Flip_Flop _1 (.clk(clock_1_out), .D(_1_qn), .Q(_1_q), .Qn(_1_qn), .preset(button_1_out));  // open: en, reset
  D_Flip_Flop _0 (.clk(clock_1_out), .D(1'b0), .reset(button_1_out));  // open: Q, Qn, preset, en
endmodule
