// Logisim project impares1-7.circ as structural Verilog: 1 circuit, main circuit main
module main (
);

  wire _1_q, button_1_out, clock_1_out, not_1_out;

  Clock clock_1 (.out(clock_1_out));
  Button button_1 (.out(button_1_out));
  J_K_Flip_Flop _2 (.J(_1_q), .clk(clock_1_out), .K(_1_q), .reset(button_1_out));  // open: Q, Qn, preset, en
  J_K_Flip_Flop _1 (.J(1'b1), .clk(clock_1_out), .K(1'b1), .Q(_1_q), .reset(button_1_out));  // open: Qn, preset, en
  not not_1 (not_1_out, 1'b1);
  J_K_Flip_Flop _0 (.J(1'b1), .clk(clock_1_out), .K(not_1_out), .preset(button_1_out));  // open: Q, Qn, en, reset
endmodule
