// Logisim project sequencia0-9.circ as structural Verilog: 1 circuit, main circuit main
module main (
);

  wire _0_q, _1_q, _2_q, _3_q, and_1_out, and_2_out, and_3_out, button_1_out, clock_1_out;

  Clock clock_1 (.out(clock_1_out));
  Button button_1 (.out(button_1_out));
  and and_1 (and_1_out, _2_q, _1_q, _0_q);
  J_K_Flip_Flop _3 (
    .J(and_1_out), .clk(clock_1_out), .K(_0_q), .Q(_3_q), .reset(button_1_out));  // open: Qn, preset, en
  and and_2 (and_2_out, _1_q, _0_q);
  J_K_Flip_Flop _2 (
    .J(and_2_out), .clk(clock_1_out), .K(and_2_out), .Q(_2_q), .reset(button_1_out));  // open: Qn, preset, en
  and and_3 (and_3_out, _0_q, ~_3_q);  // AND_Gate
  J_K_Flip_Flop _1 (
    .J(and_3_out), .clk(clock_1_out), .K(_0_q), .Q(_1_q), .reset(button_1_out));  // open: Qn, preset, en
  J_K_Flip_Flop _0 (.J(1'b1), .clk(clock_1_out), .K(1'b1), .Q(_0_q), .reset(button_1_out));  // open: Qn, preset, en
endmodule
